# Fritzing sketch RelayShield (saved by Fritzing 0.9.3b)
circuit board: 3.14989cm x 5.45009cm
breadboards: 1

parts:
  Part1 = Arduino Uno (Rev3)
  J1 = Screw terminal - 2 pins [package=THT]
  J2 = Screw terminal - 2 pins [package=THT]
  J3 = Screw terminal - 2 pins [package=THT]
  J4 = Screw terminal - 2 pins [package=THT]
  J5 = Screw terminal - 2 pins [package=THT]
  J6 = Screw terminal - 2 pins [package=THT]

nets:
  N1: Part1.D8, J2.pin1
  N2: Part1.D9_PWM, J2.pin2
  N3: Part1.D10_PWM/SS, J1.pin1
  N4: Part1.D11_PWM/MOSI, J1.pin2
  N5: Part1.D12/MISO, J6.pin1
  N6: Part1.D13/SCK, J6.pin2
  N7: Part1.D6_PWM, J5.pin1
  N8: Part1.D7, J5.pin2
  N9: Part1.5V, J3.pin1
  N10: Part1.GND, J3.pin2, J4.pin1
  N11: Part1.VIN, J4.pin2
