# Fritzing sketch mcopy_MONO_JK99_shield (saved by Fritzing 0.9.5d)
circuit board: 3.08021cm x 5.25502cm
breadboards: 1

parts:
  Part1 = Arduino Uno (Rev3)
  J1 = Screw terminal - 2 pins [package=THT]
  J2 = Screw terminal - 2 pins [package=THT]
  J3 = Screw terminal - 2 pins [package=THT]
  J4 = Screw terminal - 2 pins [package=THT]
  FWD = Screw terminal - 2 pins [package=THT]
  BWD = Screw terminal - 2 pins [package=THT]
  MICRO = Screw terminal - 2 pins [package=THT]
  220 = Resistor [tolerance=±5% resistance=220 package=THT]
  220_2 = Resistor [tolerance=±5% resistance=220 package=THT]

nets:
  N1: Part1.D8, FWD.pin1
  N2: Part1.D9_PWM, BWD.pin1
  N3: Part1.D10_PWM/SS, MICRO.pin1
  N4: Part1.GND, J2.pin2, J4.pin1, J4.pin2, MICRO.pin2, 220.Pin_1, 220_2.Pin_1
  N5: Part1.D3_PWM, J1.pin1
  N6: Part1.D4, J1.pin2
  N7: Part1.D5_PWM, J3.pin1
  N8: Part1.D6_PWM, J3.pin2
  N9: Part1.5V, J2.pin1
  N10: FWD.pin2, 220.Pin_0
  N11: BWD.pin2, 220_2.Pin_0

notes:
  proj adv [3]
  proj rew [4]
  takeup adv [5]
  takeup rew [6]
  [5V]
  [GND]
  mcopy JK100.2
