# Fritzing sketch mcopy_projector_breakout_board (saved by Fritzing 0.9.3b)
circuit board: 4.03925cm x 6.93685cm
breadboards: 1

parts:
  220 = Resistor [tolerance=±5% resistance=220 package=THT]
  220_2 = Resistor [tolerance=±5% resistance=220 package=THT]
  10K = Resistor [tolerance=±5% resistance=220 package=THT]
  10K_2 = Resistor [tolerance=±5% resistance=10k package=THT]
  10K_3 = Resistor [tolerance=±5% resistance=10k package=THT]
  220_3 = Resistor [tolerance=±5% resistance=220 package=THT]
  220_4 = Resistor [tolerance=±5% resistance=220 package=THT]
  10K_4 = Resistor [tolerance=±5% resistance=10k package=THT]
  J1 = screw terminal, 2 pins
  J2 = screw terminal, 2 pins
  J3 = screw terminal, 2 pins
  J4 = screw terminal, 2 pins
  J5 = screw terminal, 2 pins
  J6 = screw terminal, 2 pins
  J7 = screw terminal, 2 pins
  J8 = screw terminal, 2 pins
  J9 = screw terminal, 2 pins
  J10 = screw terminal, 2 pins
  J11 = screw terminal, 2 pins
  J12 = screw terminal, 2 pins
  J13 = screw terminal, 2 pins

nets:
  N1: 220.Pin_0, J1.pin2
  N2: 220.Pin_1, J9.pin1
  N3: 220_2.Pin_0, J2.pin2
  N4: 220_2.Pin_1, J9.pin2
  N5: 10K.Pin_0, J3.pin1, J10.pin1
  N6: 10K.Pin_1, 10K_2.Pin_1, 10K_3.Pin_1, 10K_4.Pin_1, J1.pin1, J2.pin1, J5.pin1, J6.pin1, J13.pin1
  N7: 10K_2.Pin_0, J4.pin1, J10.pin2
  N8: 10K_3.Pin_0, J8.pin1, J12.pin2
  N9: 220_3.Pin_0, J5.pin2
  N10: 220_3.Pin_1, J11.pin1
  N11: 220_4.Pin_0, J6.pin2
  N12: 220_4.Pin_1, J11.pin2
  N13: 10K_4.Pin_0, J7.pin1, J12.pin1
  N14: J3.pin2, J4.pin2, J7.pin2, J8.pin2, J13.pin2
