# Fritzing sketch mcopy_projector_mega_shield (saved by Fritzing 0.9.5d)
circuit board: 3.46193cm x 5.47511cm
breadboards: 1

parts:
  J1 = Screw terminal - 2 pins [package=THT]
  J2 = Screw terminal - 2 pins [package=THT]
  J3 = Screw terminal - 2 pins [package=THT]
  J4 = Screw terminal - 2 pins [package=THT]
  220 = Resistor [tolerance=±5% resistance=220 package=THT]
  10K = Resistor [tolerance=±5% resistance=10k package=THT]
  220_2 = Resistor [tolerance=±5% resistance=220 package=THT]
  10K_2 = Resistor [tolerance=±5% resistance=10k package=THT]
  Part1 = Arduino Mega ADK (Rev3)
  J5 = Basic Servo
  J6 = Screw terminal - 2 pins [package=THT]
  J7 = Screw terminal - 2 pins [package=THT]
  J8 = Screw terminal - 2 pins [package=THT]

nets:
  N1: J1.pin1, Part1.D18/TX1
  N2: J1.pin2, 10K.Pin_0, Part1.A8
  N3: J2.pin1, Part1.D20/SDA
  N4: J2.pin2, 220.Pin_0
  N5: J3.pin1, Part1.D17/RX2
  N6: J3.pin2, 10K_2.Pin_0, Part1.A9
  N7: J4.pin1, Part1.D19/RX1
  N8: J4.pin2, 220_2.Pin_0
  GND: 220.Pin_1, 10K.Pin_1, 220_2.Pin_1, 10K_2.Pin_1, Part1.GND, J5.gnd, J7.pin1, J7.pin2
  N9: Part1.D21/SCL, J5.pulse
  5V: Part1.5V, J5.vcc
  N10: Part1.D22, J6.pin2
  N11: Part1.D24, J6.pin1
  N12: Part1.D26, J8.pin2
  N13: Part1.D28, J8.pin1
